// Logisim project cpu24.circ as structural Verilog: 11 circuits, main circuit ◇单周期MIPS
module \单周期MIPS  (
  output RegWrite,
  output MemWrite,
  output [31:0] PC,
  output [31:0] IR,
  output [31:0] RDin,
  output [31:0] MDin
);

  wire ALUToReg, and_1_out, and_2_out, and_3_out, and_4_out, bltz, ByteOrWord, CLK, comparator_1_eq, display,
       Go, IR1, IR2, IR3, mips_alu_1_equal, not_2_out, not_3_out, not_4_out, pause, pcEnable, SignedExt,
       syscall, W1, W2, W3, \单周期硬布线控制器_1_alu_src , \单周期硬布线控制器_1_beq , \单周期硬布线控制器_1_bne ,
       \单周期硬布线控制器_1_memtoreg , \条件分支 ;
  wire [1:0] \单周期硬布线控制器_1_jal , \单周期硬布线控制器_1_jr ;
  wire [3:0] adder_1_out, \单周期硬布线控制器_1_alu_op ;
  wire [4:0] multiplexer_2_out, multiplexer_3_out, multiplexer_4_out;
  wire [7:0] multiplexer_10_out, multiplexer_11_out, multiplexer_11_out_2, multiplexer_11_out_3,
       multiplexer_11_out_4;
  wire [15:0] \总周期数 ;
  wire [27:0] adder_1_out_2;
  wire [31:0] adder_2_out, ALUResult, bit_extender_1_out, bit_extender_2_out, bit_extender_3_out, LedData,
       multiplexer_1_out, multiplexer_5_out, multiplexer_7_out, multiplexer_8_out, multiplexer_9_out,
       ram_1_data, shifter_1_out, sysreg;

  Clock #(.highDuration(1), .lowDuration(1)) clock_1 (.out(CLK));
  Button _1 (.out(IR1));
  Button _2 (.out(IR2));
  Button _3 (.out(IR3));
  Button \u_继续运行  (.out(Go));
  LED #(.active("true")) led_1 (.in(W1));
  LED #(.active("true")) led_2 (.in(W2));
  LED #(.active("true")) led_3 (.in(W3));
  Hex_Digit_Display hex_digit_display_1 (.value(LedData[31:28]));  // open: dp
  // Probe on multiplexer_1_out
  Multiplexer #(.select(3), .width(32), .disabled("Z"), .enable("false")) multiplexer_1 (
    .in0({adder_1_out, adder_1_out_2}), .in1(sysreg), .in2({adder_1_out, IR[25:0], 2'b00}), .in3(sysreg),
    .in4(adder_2_out), .in5({adder_1_out, adder_1_out_2}), .in6({adder_1_out, adder_1_out_2}),
    .in7({adder_1_out, adder_1_out_2}), .out(multiplexer_1_out), .sel({\条件分支 , \单周期硬布线控制器_1_jr }));
  Register #(.width(32), .trigger("rising"), .Select("low")) u_PC (
    .D(multiplexer_1_out), .en(pcEnable), .Q(PC), .clk(CLK));  // open: clr
  Hex_Digit_Display hex_digit_display_2 (.value(LedData[27:24]));  // open: dp
  Hex_Digit_Display hex_digit_display_3 (.value(LedData[23:20]));  // open: dp
  Hex_Digit_Display hex_digit_display_4 (.value(LedData[15:12]));  // open: dp
  Hex_Digit_Display hex_digit_display_5 (.value(LedData[19:16]));  // open: dp
  Adder #(.width(32)) adder_1 (.a(PC), .b(32'h4), .out({adder_1_out, adder_1_out_2}));  // open: cin, cout
  Hex_Digit_Display hex_digit_display_6 (.value(LedData[7:4]));  // open: dp
  Hex_Digit_Display hex_digit_display_7 (.value(LedData[11:8]));  // open: dp
  // Probe on \总周期数 
  ROM #(.addrWidth(10), .dataWidth(32), .Select("high")) rom_1 (.addr(PC[11:2]), .data(IR));
  Hex_Digit_Display hex_digit_display_8 (.value(LedData[3:0]));  // open: dp
  assign bit_extender_1_out = {{16{IR[15]}}, IR[15:0]};  // Bit_Extender bit_extender_1
  \单周期硬布线控制器  \u_单周期硬布线控制器_1  (
    .Func(IR[5:0]), .OP(IR[31:26]), .ALU_OP(\单周期硬布线控制器_1_alu_op ), .MemToReg(\单周期硬布线控制器_1_memtoreg ),
    .MemWrite(MemWrite), .ALU_SRC(\单周期硬布线控制器_1_alu_src ), .RegWrite(RegWrite), .SysCALL(syscall),
    .SignedExt(SignedExt), .RegDst(\单周期硬布线控制器_1_jal [1]), .JR(\单周期硬布线控制器_1_jr [0]),
    .JMP(\单周期硬布线控制器_1_jr [1]), .Beq(\单周期硬布线控制器_1_beq ), .JAL(\单周期硬布线控制器_1_jal [0]), .Bne(\单周期硬布线控制器_1_bne ));
  Shifter #(.width(32), .shift("ll")) shifter_1 (.in(bit_extender_1_out), .\dist (5'b00010), .out(shifter_1_out));
  Multiplexer #(.select(1), .width(5), .disabled("Z"), .enable("false")) multiplexer_2 (
    .in0(IR[20:16]), .in1(5'b00010), .out(multiplexer_2_out), .sel(syscall));
  Adder #(.width(32)) adder_2 (
    .a(shifter_1_out), .b({adder_1_out, adder_1_out_2}), .out(adder_2_out));  // open: cin, cout
  // Probe on multiplexer_3_out
  Multiplexer #(.select(1), .width(5), .disabled("Z"), .enable("false")) multiplexer_3 (
    .in0(IR[25:21]), .in1(5'b00100), .out(multiplexer_3_out), .sel(syscall));
  // Probe on multiplexer_4_out
  Multiplexer #(.select(2), .width(5), .disabled("Z"), .enable("false")) multiplexer_4 (
    .in0(IR[20:16]), .in1({5{1'b1}}), .in2(IR[15:11]), .in3({5{1'b1}}), .out(multiplexer_4_out),
    .sel(\单周期硬布线控制器_1_jal ));
  Multiplexer #(.select(1), .width(32), .disabled("Z"), .enable("false")) multiplexer_5 (
    .in0(multiplexer_9_out), .in1(ALUResult), .out(multiplexer_5_out), .sel(ALUToReg));
  // Probe on RDin
  // Probe on multiplexer_2_out
  Multiplexer #(.select(1), .width(32), .disabled("Z"), .enable("false")) multiplexer_6 (
    .in0(multiplexer_5_out), .in1({adder_1_out, adder_1_out_2}), .out(RDin), .sel(\单周期硬布线控制器_1_jal [0]));
  assign bit_extender_2_out = {{16{1'b0}}, IR[15:0]};  // Bit_Extender bit_extender_2
  MIPS_Regifile mips_regifile_1 (
    .Din(RDin), .Clk(CLK), .R1(MDin), .R2(sysreg), .WE(RegWrite), .W_num(multiplexer_4_out),
    .R1_num(multiplexer_2_out), .R2_num(multiplexer_3_out));
  Multiplexer #(.select(1), .width(32), .disabled("Z"), .enable("false")) multiplexer_7 (
    .in0(bit_extender_2_out), .in1(bit_extender_1_out), .out(multiplexer_7_out), .sel(SignedExt));
  // Probe on multiplexer_8_out
  Multiplexer #(.select(1), .width(32), .disabled("Z"), .enable("false")) multiplexer_8 (
    .in0(MDin), .in1(multiplexer_7_out), .out(multiplexer_8_out), .sel(\单周期硬布线控制器_1_alu_src ));
  Multiplexer #(.select(1), .width(32), .disabled("Z"), .enable("false")) multiplexer_9 (
    .in0({multiplexer_11_out_4, multiplexer_11_out_3, multiplexer_11_out_2, multiplexer_11_out}),
    .in1(bit_extender_3_out), .out(multiplexer_9_out), .sel(ByteOrWord));
  MIPS_ALU mips_alu_1 (
    .X(sysreg), .Y(multiplexer_8_out), .AluOP(\单周期硬布线控制器_1_alu_op ), .Equal(mips_alu_1_equal),
    .Result(ALUResult), .shamt(IR[10:6]));  // open: Result_2
  assign bit_extender_3_out = {{24{multiplexer_10_out[7]}}, multiplexer_10_out};  // Bit_Extender bit_extender_3
  // Probe on bit_extender_3_out
  not not_1 (pcEnable, and_1_out);
  and and_1 (and_1_out, ~Go, pause);  // AND_Gate
  and and_2 (and_2_out, \单周期硬布线控制器_1_bne , not_2_out);
  not not_2 (not_2_out, mips_alu_1_equal);
  // Probe on multiplexer_11_out
  // Probe on ALUResult[1:0]
  Multiplexer #(.select(2), .width(8), .disabled("Z"), .enable("false")) multiplexer_10 (
    .in0(multiplexer_11_out), .in1(multiplexer_11_out_2), .in2(multiplexer_11_out_3),
    .in3(multiplexer_11_out_4), .out(multiplexer_10_out), .sel(ALUResult[1:0]));
  and and_3 (and_3_out, \单周期硬布线控制器_1_beq , mips_alu_1_equal);
  and and_4 (and_4_out, bltz, sysreg[31]);
  not not_3 (not_3_out, MemWrite);
  // Probe on {multiplexer_11_out_4, multiplexer_11_out_3, multiplexer_11_out_2, multiplexer_11_out}
  or or_1 (\条件分支 , and_3_out, and_4_out, and_2_out);
  RAM #(.addrWidth(10), .dataWidth(32), .bus("separate"), .Select("high")) ram_1 (
    .addr(ALUResult[11:2]), .din(MDin), .data(ram_1_data), .str(MemWrite), .clk(CLK), .ld(not_3_out));  // open: sel, clr
  Comparator #(.width(32), .mode("twosComplement")) comparator_1 (
    .a(MDin), .b(32'h22), .eq(comparator_1_eq));  // open: gt, lt
  not not_4 (not_4_out, comparator_1_eq);
  Multiplexer #(.select(1), .width(32), .disabled("Z"), .enable("false")) multiplexer_11 (
    .in0(ALUResult), .in1(ram_1_data),
    .out({multiplexer_11_out_4, multiplexer_11_out_3, multiplexer_11_out_2, multiplexer_11_out}),
    .sel(\单周期硬布线控制器_1_memtoreg ));
  and and_5 (display, comparator_1_eq, syscall);
  and and_6 (pause, syscall, not_4_out);
  Counter #(.width(16), .max('hffff), .ongoal("wrap"), .trigger("rising"), .behavior("old")) counter_1 (
    .count(pcEnable), .Q(\总周期数 ), .clk(CLK));  // open: load, D, carry, clr, preset
  Register #(.width(32), .trigger("rising"), .Select("low")) register_1 (
    .D(sysreg), .en(display), .Q(LedData), .clk(CLK));  // open: clr
  NEW_CONTRLLER new_contrller_1 (
    .OP0(IR[26]), .OP1(IR[27]), .OP2(IR[28]), .OP3(IR[29]), .OP4(IR[30]), .OP5(IR[31]), .F0(IR[0]),
    .F1(IR[1]), .F2(IR[2]), .F3(IR[3]), .F4(IR[4]), .F5(IR[5]), .byteorword(ByteOrWord), .bltz(bltz),
    .ALutoREg(ALUToReg));

  // Other names for the same wires on the sheet: Funct[5:0] = IR[5:0]; OP[5:0] = IR[31:26]; syspara[31:0] = MDin

  // Notes on the sheet:
  //   中断源
  //   中断等待指示
  //   总复位信号应将除ROM以外所有存储组件全部清零
  //   条件分支
  //   JMP
  //   JR
  //   pc+4
  //   jumpAddr
  //   pc+4+imm
  //   register
  //   数码管输出
  //   指令存储器
  //   数码管输出应该用寄存器锁存，否则显示数据只能一闪而过
  //   指令字
  //   contents of rom_1 (hex, n*v repeats v):
  //   2011fff1 112020 20020022 c 22310001 620fffb 2002000a c
  //   pc+4
  //   rs
  //   base
  //   rt
  //   rd
  //   shamt
  //   Imm/offset
  //   jumpAddr
  //   JMP
  //   JR
  //   OP
  //   Func
  //   Syscall
  //   Beq
  //   Bne
  //   MemToReg
  //   MemWrite
  //   AluOP
  //   AluSrcB
  //   RegWrite
  //   JAL
  //   RegDst
  //   为方便自动评测，需要输出PC，IR，寄存器文件写入端口RDin，内存写入端口MDin等信号
  //   rs
  //   rt
  //   rs
  //   rt
endmodule

// 单周期硬布线控制器
module \单周期硬布线控制器  (
  input  [5:0] OP,
  input  [5:0] Func,
  output [3:0] ALU_OP,
  output MemToReg,
  output MemWrite,
  output ALU_SRC,
  output RegWrite,
  output SysCALL,
  output SignedExt,
  output RegDst,
  output Beq,
  output Bne,
  output JR,
  output JMP,
  output JAL
);

  // Probe on OP
  // Probe on Func
  \运算控制器自动生成  \u_运算控制器自动生成_1  (
    .OP0(OP[0]), .OP1(OP[1]), .OP2(OP[2]), .OP3(OP[3]), .OP4(OP[4]), .OP5(OP[5]), .F0(Func[0]), .F1(Func[1]),
    .F2(Func[2]), .F3(Func[3]), .F4(Func[4]), .F5(Func[5]), .S0(ALU_OP[0]), .S1(ALU_OP[1]), .S2(ALU_OP[2]),
    .S3(ALU_OP[3]));
  \控制信号自动生成  \u_控制信号自动生成_1  (
    .OP0(OP[0]), .OP1(OP[1]), .OP2(OP[2]), .OP3(OP[3]), .OP4(OP[4]), .OP5(OP[5]), .F0(Func[0]), .F1(Func[1]),
    .F2(Func[2]), .F3(Func[3]), .F4(Func[4]), .F5(Func[5]), .MemToReg(MemToReg), .MemWrite(MemWrite),
    .ALU_SRC(ALU_SRC), .RegWrite(RegWrite), .SysCALL(SysCALL), .SignedExt(SignedExt), .RegDst(RegDst),
    .BEQ(Beq), .BNE(Bne), .JR(JR), .JMP(JMP), .JAL(JAL));

  // Other names for the same wires on the sheet: OP_CODE[5:0] = OP

  // Notes on the sheet:
  //   运算器控制器，根据指令生成运算器功能选择信号
  //   控制信号生成，产生数据通路需要的其他控制信号
endmodule

// 运算器控制器
module \运算控制器自动生成  (
  input  OP0,
  input  OP1,
  input  OP2,
  input  OP3,
  input  OP4,
  input  OP5,
  input  F0,
  input  F1,
  input  F2,
  input  F3,
  input  F4,
  input  F5,
  output S0,
  output S1,
  output S2,
  output S3
);

  wire and_1_out, and_2_out, and_3_out, and_4_out, and_5_out, and_6_out, and_7_out, and_8_out, and_9_out,
       and_10_out, and_11_out, and_12_out, and_13_out, and_14_out, and_15_out, and_16_out, and_17_out,
       and_18_out, and_19_out, and_20_out, and_21_out, and_22_out, and_23_out, and_24_out, and_25_out,
       and_26_out, and_27_out, and_28_out, and_29_out, not_1_out, not_2_out, not_3_out, not_4_out, not_5_out,
       not_6_out, not_7_out, not_8_out, not_9_out, not_10_out, not_11_out, not_12_out, not_13_out,
       not_14_out, not_15_out, not_16_out, not_17_out, not_18_out, not_19_out, not_20_out, not_21_out,
       not_22_out, not_23_out, not_24_out, not_25_out, not_26_out, not_27_out, not_28_out, not_29_out,
       not_30_out, not_31_out, not_32_out, not_33_out, not_34_out, not_35_out, not_36_out, not_37_out,
       not_38_out, not_39_out, not_40_out, not_41_out, not_42_out, not_43_out, not_44_out, not_45_out,
       not_46_out, not_47_out, not_48_out, not_49_out, not_50_out, not_51_out, not_52_out, not_53_out,
       not_54_out, not_55_out, not_56_out, not_57_out, not_58_out, not_59_out, not_60_out, not_61_out,
       not_62_out, not_63_out, not_64_out, not_65_out, not_66_out, not_67_out, not_68_out, not_69_out,
       not_70_out, not_71_out, not_72_out, not_73_out, not_74_out, not_75_out, not_76_out, not_77_out,
       not_78_out, not_79_out, not_80_out, not_81_out, not_82_out, not_83_out, not_84_out, not_85_out,
       not_86_out, not_87_out, not_88_out, not_89_out, not_90_out, not_91_out, not_92_out, not_93_out,
       not_94_out, not_95_out, not_96_out, not_97_out, not_98_out, not_99_out, not_100_out, not_101_out,
       not_102_out, not_103_out, not_104_out, not_105_out, not_106_out, not_107_out, not_108_out,
       not_109_out, not_110_out, not_111_out, not_112_out, not_113_out, not_114_out, not_115_out,
       not_116_out, not_117_out, not_118_out, not_119_out, not_120_out, not_121_out, not_122_out,
       not_123_out, not_124_out, not_125_out, not_126_out, not_127_out, not_128_out, not_129_out,
       not_130_out, not_131_out, not_132_out, not_133_out, not_134_out, not_135_out, not_136_out,
       not_137_out, not_138_out, not_139_out, not_140_out, not_141_out, not_142_out, not_143_out,
       not_144_out, not_145_out, not_146_out, not_147_out, not_148_out, not_149_out, not_150_out,
       not_151_out, not_152_out, not_153_out, not_154_out, not_155_out, not_156_out, not_157_out,
       not_158_out, not_159_out, not_160_out, not_161_out, not_162_out, not_163_out, not_164_out,
       not_165_out, not_166_out, not_167_out;

  not not_1 (not_1_out, OP0);
  not not_2 (not_2_out, OP1);
  not not_3 (not_3_out, OP2);
  not not_4 (not_4_out, OP4);
  not not_5 (not_5_out, OP5);
  not not_6 (not_6_out, F0);
  not not_7 (not_7_out, F1);
  not not_8 (not_8_out, F3);
  not not_9 (not_9_out, F4);
  not not_10 (not_10_out, OP0);
  not not_11 (not_11_out, OP1);
  not not_12 (not_12_out, OP2);
  not not_13 (not_13_out, OP4);
  not not_14 (not_14_out, OP5);
  not not_15 (not_15_out, F1);
  not not_16 (not_16_out, F2);
  not not_17 (not_17_out, F3);
  not not_18 (not_18_out, F4);
  not not_19 (not_19_out, OP0);
  not not_20 (not_20_out, OP1);
  not not_21 (not_21_out, OP2);
  not not_22 (not_22_out, OP4);
  not not_23 (not_23_out, OP5);
  not not_24 (not_24_out, F0);
  not not_25 (not_25_out, F2);
  not not_26 (not_26_out, F4);
  not not_27 (not_27_out, OP0);
  not not_28 (not_28_out, OP1);
  not not_29 (not_29_out, OP2);
  not not_30 (not_30_out, OP4);
  not not_31 (not_31_out, OP5);
  not not_32 (not_32_out, F2);
  not not_33 (not_33_out, F3);
  not not_34 (not_34_out, F4);
  not not_35 (not_35_out, F5);
  not not_36 (not_36_out, OP0);
  not not_37 (not_37_out, OP4);
  not not_38 (not_38_out, OP5);
  not not_39 (not_39_out, OP1);
  not not_40 (not_40_out, OP2);
  not not_41 (not_41_out, OP4);
  not not_42 (not_42_out, OP5);
  not not_43 (not_43_out, OP0);
  not not_44 (not_44_out, OP1);
  not not_45 (not_45_out, OP3);
  not not_46 (not_46_out, OP4);
  not not_47 (not_47_out, OP2);
  not not_48 (not_48_out, OP4);
  not not_49 (not_49_out, OP0);
  not not_50 (not_50_out, OP1);
  not not_51 (not_51_out, OP2);
  not not_52 (not_52_out, OP3);
  not not_53 (not_53_out, OP4);
  not not_54 (not_54_out, OP0);
  not not_55 (not_55_out, OP1);
  not not_56 (not_56_out, OP2);
  not not_57 (not_57_out, OP3);
  not not_58 (not_58_out, OP4);
  not not_59 (not_59_out, OP5);
  not not_60 (not_60_out, F0);
  not not_61 (not_61_out, F1);
  not not_62 (not_62_out, F3);
  not not_63 (not_63_out, F4);
  not not_64 (not_64_out, OP0);
  not not_65 (not_65_out, OP1);
  not not_66 (not_66_out, OP2);
  not not_67 (not_67_out, OP3);
  not not_68 (not_68_out, OP4);
  not not_69 (not_69_out, OP5);
  not not_70 (not_70_out, F0);
  not not_71 (not_71_out, F2);
  not not_72 (not_72_out, F3);
  not not_73 (not_73_out, F4);
  not not_74 (not_74_out, OP0);
  not not_75 (not_75_out, OP1);
  not not_76 (not_76_out, OP2);
  not not_77 (not_77_out, OP3);
  not not_78 (not_78_out, OP4);
  not not_79 (not_79_out, OP5);
  not not_80 (not_80_out, F0);
  not not_81 (not_81_out, F2);
  not not_82 (not_82_out, F4);
  not not_83 (not_83_out, OP0);
  not not_84 (not_84_out, OP1);
  not not_85 (not_85_out, OP2);
  not not_86 (not_86_out, OP3);
  not not_87 (not_87_out, OP4);
  not not_88 (not_88_out, OP5);
  not not_89 (not_89_out, F3);
  not not_90 (not_90_out, F4);
  not not_91 (not_91_out, OP0);
  not not_92 (not_92_out, OP1);
  not not_93 (not_93_out, OP4);
  not not_94 (not_94_out, OP5);
  not not_95 (not_95_out, OP0);
  not not_96 (not_96_out, OP2);
  not not_97 (not_97_out, OP4);
  not not_98 (not_98_out, OP5);
  not not_99 (not_99_out, OP0);
  not not_100 (not_100_out, OP1);
  not not_101 (not_101_out, OP2);
  not not_102 (not_102_out, OP4);
  not not_103 (not_103_out, OP5);
  not not_104 (not_104_out, F0);
  not not_105 (not_105_out, F1);
  not not_106 (not_106_out, F3);
  not not_107 (not_107_out, F4);
  not not_108 (not_108_out, OP0);
  not not_109 (not_109_out, OP1);
  not not_110 (not_110_out, OP2);
  not not_111 (not_111_out, OP4);
  not not_112 (not_112_out, OP5);
  not not_113 (not_113_out, F2);
  not not_114 (not_114_out, F3);
  not not_115 (not_115_out, F4);
  not not_116 (not_116_out, OP0);
  not not_117 (not_117_out, OP1);
  not not_118 (not_118_out, OP2);
  not not_119 (not_119_out, OP4);
  not not_120 (not_120_out, OP5);
  not not_121 (not_121_out, F2);
  not not_122 (not_122_out, F4);
  not not_123 (not_123_out, OP0);
  not not_124 (not_124_out, OP1);
  not not_125 (not_125_out, OP4);
  not not_126 (not_126_out, OP5);
  not not_127 (not_127_out, OP0);
  not not_128 (not_128_out, OP1);
  not not_129 (not_129_out, OP3);
  not not_130 (not_130_out, OP2);
  not not_131 (not_131_out, OP4);
  not not_132 (not_132_out, OP5);
  not not_133 (not_133_out, OP2);
  not not_134 (not_134_out, OP4);
  not not_135 (not_135_out, OP0);
  not not_136 (not_136_out, OP1);
  not not_137 (not_137_out, OP2);
  not not_138 (not_138_out, OP3);
  not not_139 (not_139_out, OP4);
  not not_140 (not_140_out, OP0);
  not not_141 (not_141_out, OP1);
  not not_142 (not_142_out, OP2);
  not not_143 (not_143_out, OP3);
  not not_144 (not_144_out, OP4);
  not not_145 (not_145_out, OP5);
  not not_146 (not_146_out, F2);
  not not_147 (not_147_out, F4);
  not not_148 (not_148_out, OP0);
  not not_149 (not_149_out, OP1);
  not not_150 (not_150_out, OP2);
  not not_151 (not_151_out, OP3);
  not not_152 (not_152_out, OP4);
  not not_153 (not_153_out, OP5);
  not not_154 (not_154_out, F3);
  not not_155 (not_155_out, F4);
  not not_156 (not_156_out, OP0);
  not not_157 (not_157_out, OP1);
  not not_158 (not_158_out, OP3);
  not not_159 (not_159_out, OP0);
  not not_160 (not_160_out, OP4);
  not not_161 (not_161_out, OP5);
  not not_162 (not_162_out, OP2);
  not not_163 (not_163_out, OP4);
  not not_164 (not_164_out, OP5);
  not not_165 (not_165_out, OP1);
  not not_166 (not_166_out, OP4);
  not not_167 (not_167_out, OP5);
  and and_1 (and_1_out, not_1_out, not_2_out, not_3_out, not_4_out, not_5_out, not_6_out, not_7_out, not_8_out, not_9_out, F5);
  and and_2 (and_2_out, not_10_out, not_11_out, not_12_out, not_13_out, not_14_out, not_15_out, not_16_out, not_17_out, not_18_out, F5);
  and and_3 (and_3_out, not_19_out, not_20_out, not_21_out, not_22_out, not_23_out, not_24_out, F1, not_25_out, F3, not_26_out, F5);
  and and_4 (and_4_out, not_27_out, not_28_out, not_29_out, not_30_out, not_31_out, F0, F1, not_32_out, not_33_out, not_34_out, not_35_out);
  and and_5 (and_5_out, not_36_out, OP3, not_37_out, not_38_out);
  and and_6 (and_6_out, not_39_out, not_40_out, OP3, not_41_out, not_42_out);
  and and_7 (and_7_out, not_43_out, not_44_out, OP2, not_45_out, not_46_out, OP5);
  and and_8 (and_8_out, OP0, OP1, not_47_out, not_48_out, OP5);
  and and_9 (and_9_out, not_49_out, not_50_out, not_51_out, not_52_out, not_53_out, OP5);
  and and_10 (and_10_out, not_54_out, not_55_out, not_56_out, not_57_out, not_58_out, not_59_out, not_60_out, not_61_out, F2, not_62_out, not_63_out, F5);
  and and_11 (and_11_out, not_64_out, not_65_out, not_66_out, not_67_out, not_68_out, not_69_out, not_70_out, F1, not_71_out, not_72_out, not_73_out);
  and and_12 (and_12_out, not_74_out, not_75_out, not_76_out, not_77_out, not_78_out, not_79_out, not_80_out, F1, not_81_out, not_82_out, F5);
  and and_13 (and_13_out, not_83_out, not_84_out, not_85_out, not_86_out, not_87_out, not_88_out, F0, F1, not_89_out, not_90_out, F5);
  and and_14 (and_14_out, not_91_out, not_92_out, OP2, OP3, not_93_out, not_94_out);
  and and_15 (and_15_out, not_95_out, OP1, not_96_out, OP3, not_97_out, not_98_out);
  and and_16 (and_16_out, not_99_out, not_100_out, not_101_out, not_102_out, not_103_out, not_104_out, not_105_out, not_106_out, not_107_out, F5);
  and and_17 (and_17_out, not_108_out, not_109_out, not_110_out, not_111_out, not_112_out, not_113_out, not_114_out, not_115_out, F5);
  and and_18 (and_18_out, not_116_out, not_117_out, not_118_out, not_119_out, not_120_out, F0, F1, not_121_out, not_122_out, F5);
  and and_19 (and_19_out, not_123_out, not_124_out, OP3, not_125_out, not_126_out);
  and and_20 (and_20_out, not_127_out, not_128_out, OP2, not_129_out, OP5);
  and and_21 (and_21_out, OP0, not_130_out, OP3, not_131_out, not_132_out);
  and and_22 (and_22_out, OP0, OP1, not_133_out, not_134_out, OP5);
  and and_23 (and_23_out, not_135_out, not_136_out, not_137_out, not_138_out, not_139_out, OP5);
  and and_24 (and_24_out, not_140_out, not_141_out, not_142_out, not_143_out, not_144_out, not_145_out, F1, not_146_out, F3, not_147_out, F5);
  and and_25 (and_25_out, not_148_out, not_149_out, not_150_out, not_151_out, not_152_out, not_153_out, F0, F2, not_154_out, not_155_out, F5);
  and and_26 (and_26_out, not_156_out, not_157_out, OP2, not_158_out, OP4, OP5);
  and and_27 (and_27_out, not_159_out, OP1, OP3, not_160_out, not_161_out);
  and and_28 (and_28_out, OP1, not_162_out, OP3, not_163_out, not_164_out);
  and and_29 (and_29_out, OP0, not_165_out, OP2, OP3, not_166_out, not_167_out);
  or or_1 (S0, and_1_out, and_2_out, and_3_out, and_4_out, and_5_out, and_6_out, and_7_out, and_8_out, and_9_out);
  or or_2 (S1, and_10_out, and_11_out, and_12_out, and_13_out, and_14_out, and_15_out);
  or or_3 (S2, and_16_out, and_17_out, and_18_out, and_19_out, and_20_out, and_21_out, and_22_out, and_23_out);
  or or_4 (S3, and_24_out, and_25_out, and_26_out, and_27_out, and_28_out, and_29_out);
endmodule

// 控制信号生成
module \控制信号自动生成  (
  input  OP0,
  input  OP1,
  input  OP2,
  input  OP3,
  input  OP4,
  input  OP5,
  input  F0,
  input  F1,
  input  F2,
  input  F3,
  input  F4,
  input  F5,
  output MemToReg,
  output MemWrite,
  output ALU_SRC,
  output RegWrite,
  output SysCALL,
  output SignedExt,
  output RegDst,
  output BEQ,
  output BNE,
  output JR,
  output JMP,
  output JAL
);

  wire and_1_out, and_2_out, and_3_out, and_5_out, and_6_out, and_7_out, and_8_out, and_9_out, and_10_out,
       and_11_out, and_12_out, and_13_out, and_14_out, and_15_out, and_16_out, and_17_out, and_18_out,
       and_20_out, and_21_out, and_22_out, and_23_out, and_24_out, and_25_out, and_26_out, and_27_out,
       and_31_out, and_32_out, not_1_out, not_2_out, not_3_out, not_4_out, not_5_out, not_6_out, not_7_out,
       not_8_out, not_9_out, not_10_out, not_11_out, not_12_out, not_13_out, not_14_out, not_15_out,
       not_16_out, not_17_out, not_18_out, not_19_out, not_20_out, not_21_out, not_22_out, not_23_out,
       not_24_out, not_25_out, not_26_out, not_27_out, not_28_out, not_29_out, not_30_out, not_31_out,
       not_32_out, not_33_out, not_34_out, not_35_out, not_36_out, not_37_out, not_38_out, not_39_out,
       not_40_out, not_41_out, not_42_out, not_43_out, not_44_out, not_45_out, not_46_out, not_47_out,
       not_48_out, not_49_out, not_50_out, not_51_out, not_52_out, not_53_out, not_54_out, not_55_out,
       not_56_out, not_57_out, not_58_out, not_59_out, not_60_out, not_61_out, not_62_out, not_63_out,
       not_64_out, not_65_out, not_66_out, not_67_out, not_68_out, not_69_out, not_70_out, not_71_out,
       not_72_out, not_73_out, not_74_out, not_75_out, not_76_out, not_77_out, not_78_out, not_79_out,
       not_80_out, not_81_out, not_82_out, not_83_out, not_84_out, not_85_out, not_86_out, not_87_out,
       not_88_out, not_89_out, not_90_out, not_91_out, not_92_out, not_93_out, not_94_out, not_95_out,
       not_96_out, not_97_out, not_98_out, not_99_out, not_100_out, not_101_out, not_102_out, not_103_out,
       not_104_out, not_105_out, not_106_out, not_107_out, not_108_out, not_109_out, not_110_out,
       not_111_out, not_112_out, not_113_out, not_114_out, not_115_out, not_116_out, not_117_out,
       not_118_out, not_119_out, not_120_out, not_121_out, not_122_out, not_123_out, not_124_out,
       not_125_out, not_126_out, not_127_out, not_128_out, not_129_out, not_130_out, not_131_out,
       not_132_out, not_133_out, not_134_out, not_135_out, not_136_out, not_137_out, not_138_out,
       not_139_out, not_140_out, not_141_out, not_142_out, not_143_out, not_144_out, not_145_out,
       not_146_out, not_147_out, not_148_out, not_149_out, not_150_out, not_151_out, not_152_out,
       not_153_out, not_154_out, not_155_out, not_156_out, not_157_out, not_158_out, not_159_out,
       not_160_out, not_161_out, not_162_out, not_163_out, not_164_out, not_165_out, not_166_out,
       not_167_out, not_168_out, not_169_out, not_170_out, not_171_out, not_172_out, not_173_out;

  not not_1 (not_1_out, OP0);
  not not_2 (not_2_out, OP1);
  not not_3 (not_3_out, OP3);
  not not_4 (not_4_out, OP4);
  not not_5 (not_5_out, OP2);
  not not_6 (not_6_out, OP3);
  not not_7 (not_7_out, OP4);
  not not_8 (not_8_out, OP0);
  not not_9 (not_9_out, OP1);
  not not_10 (not_10_out, OP2);
  not not_11 (not_11_out, OP3);
  not not_12 (not_12_out, OP4);
  not not_13 (not_13_out, OP2);
  not not_14 (not_14_out, OP4);
  not not_15 (not_15_out, OP0);
  not not_16 (not_16_out, OP1);
  not not_17 (not_17_out, OP3);
  not not_18 (not_18_out, OP4);
  not not_19 (not_19_out, OP0);
  not not_20 (not_20_out, OP4);
  not not_21 (not_21_out, OP5);
  not not_22 (not_22_out, OP1);
  not not_23 (not_23_out, OP4);
  not not_24 (not_24_out, OP5);
  not not_25 (not_25_out, OP2);
  not not_26 (not_26_out, OP4);
  not not_27 (not_27_out, OP5);
  not not_28 (not_28_out, OP2);
  not not_29 (not_29_out, OP4);
  not not_30 (not_30_out, OP0);
  not not_31 (not_31_out, OP1);
  not not_32 (not_32_out, OP2);
  not not_33 (not_33_out, OP3);
  not not_34 (not_34_out, OP4);
  not not_35 (not_35_out, F0);
  not not_36 (not_36_out, F1);
  not not_37 (not_37_out, F3);
  not not_38 (not_38_out, F4);
  not not_39 (not_39_out, OP0);
  not not_40 (not_40_out, OP1);
  not not_41 (not_41_out, OP2);
  not not_42 (not_42_out, OP3);
  not not_43 (not_43_out, OP4);
  not not_44 (not_44_out, F2);
  not not_45 (not_45_out, F3);
  not not_46 (not_46_out, F4);
  not not_47 (not_47_out, OP0);
  not not_48 (not_48_out, OP1);
  not not_49 (not_49_out, OP2);
  not not_50 (not_50_out, OP3);
  not not_51 (not_51_out, OP4);
  not not_52 (not_52_out, F2);
  not not_53 (not_53_out, F4);
  not not_54 (not_54_out, OP0);
  not not_55 (not_55_out, OP1);
  not not_56 (not_56_out, OP2);
  not not_57 (not_57_out, OP3);
  not not_58 (not_58_out, OP4);
  not not_59 (not_59_out, F3);
  not not_60 (not_60_out, F4);
  not not_61 (not_61_out, OP0);
  not not_62 (not_62_out, OP1);
  not not_63 (not_63_out, OP3);
  not not_64 (not_64_out, OP4);
  not not_65 (not_65_out, OP0);
  not not_66 (not_66_out, OP4);
  not not_67 (not_67_out, OP5);
  not not_68 (not_68_out, OP1);
  not not_69 (not_69_out, OP4);
  not not_70 (not_70_out, OP5);
  not not_71 (not_71_out, OP2);
  not not_72 (not_72_out, OP4);
  not not_73 (not_73_out, OP5);
  not not_74 (not_74_out, OP2);
  not not_75 (not_75_out, OP3);
  not not_76 (not_76_out, OP4);
  not not_77 (not_77_out, OP0);
  not not_78 (not_78_out, OP1);
  not not_79 (not_79_out, OP2);
  not not_80 (not_80_out, OP3);
  not not_81 (not_81_out, OP4);
  not not_82 (not_82_out, OP5);
  not not_83 (not_83_out, F0);
  not not_84 (not_84_out, F1);
  not not_85 (not_85_out, F4);
  not not_86 (not_86_out, F5);
  not not_87 (not_87_out, OP0);
  not not_88 (not_88_out, OP1);
  not not_89 (not_89_out, OP3);
  not not_90 (not_90_out, OP4);
  not not_91 (not_91_out, OP0);
  not not_92 (not_92_out, OP2);
  not not_93 (not_93_out, OP4);
  not not_94 (not_94_out, OP5);
  not not_95 (not_95_out, OP1);
  not not_96 (not_96_out, OP2);
  not not_97 (not_97_out, OP4);
  not not_98 (not_98_out, OP5);
  not not_99 (not_99_out, OP2);
  not not_100 (not_100_out, OP4);
  not not_101 (not_101_out, OP0);
  not not_102 (not_102_out, OP1);
  not not_103 (not_103_out, OP2);
  not not_104 (not_104_out, OP3);
  not not_105 (not_105_out, OP4);
  not not_106 (not_106_out, OP5);
  not not_107 (not_107_out, F0);
  not not_108 (not_108_out, F1);
  not not_109 (not_109_out, F3);
  not not_110 (not_110_out, F4);
  not not_111 (not_111_out, OP0);
  not not_112 (not_112_out, OP1);
  not not_113 (not_113_out, OP2);
  not not_114 (not_114_out, OP3);
  not not_115 (not_115_out, OP4);
  not not_116 (not_116_out, OP5);
  not not_117 (not_117_out, F2);
  not not_118 (not_118_out, F3);
  not not_119 (not_119_out, F4);
  not not_120 (not_120_out, OP0);
  not not_121 (not_121_out, OP1);
  not not_122 (not_122_out, OP2);
  not not_123 (not_123_out, OP3);
  not not_124 (not_124_out, OP4);
  not not_125 (not_125_out, OP5);
  not not_126 (not_126_out, F2);
  not not_127 (not_127_out, F4);
  not not_128 (not_128_out, OP0);
  not not_129 (not_129_out, OP1);
  not not_130 (not_130_out, OP2);
  not not_131 (not_131_out, OP3);
  not not_132 (not_132_out, OP4);
  not not_133 (not_133_out, OP5);
  not not_134 (not_134_out, F3);
  not not_135 (not_135_out, F4);
  not not_136 (not_136_out, OP0);
  not not_137 (not_137_out, OP1);
  not not_138 (not_138_out, OP3);
  not not_139 (not_139_out, OP4);
  not not_140 (not_140_out, OP5);
  not not_141 (not_141_out, OP1);
  not not_142 (not_142_out, OP3);
  not not_143 (not_143_out, OP4);
  not not_144 (not_144_out, OP5);
  not not_145 (not_145_out, OP0);
  not not_146 (not_146_out, OP1);
  not not_147 (not_147_out, OP2);
  not not_148 (not_148_out, OP3);
  not not_149 (not_149_out, OP4);
  not not_150 (not_150_out, OP5);
  not not_151 (not_151_out, F0);
  not not_152 (not_152_out, F1);
  not not_153 (not_153_out, F2);
  not not_154 (not_154_out, F4);
  not not_155 (not_155_out, F5);
  not not_156 (not_156_out, OP0);
  not not_157 (not_157_out, OP2);
  not not_158 (not_158_out, OP3);
  not not_159 (not_159_out, OP4);
  not not_160 (not_160_out, OP5);
  not not_161 (not_161_out, F0);
  not not_162 (not_162_out, F1);
  not not_163 (not_163_out, F2);
  not not_164 (not_164_out, F4);
  not not_165 (not_165_out, F5);
  not not_166 (not_166_out, OP2);
  not not_167 (not_167_out, OP3);
  not not_168 (not_168_out, OP4);
  not not_169 (not_169_out, OP5);
  not not_170 (not_170_out, OP2);
  not not_171 (not_171_out, OP3);
  not not_172 (not_172_out, OP4);
  not not_173 (not_173_out, OP5);
  and and_1 (and_1_out, not_1_out, not_2_out, OP2, not_3_out, not_4_out, OP5);
  and and_2 (and_2_out, OP0, OP1, not_5_out, not_6_out, not_7_out, OP5);
  and and_3 (and_3_out, not_8_out, not_9_out, not_10_out, not_11_out, not_12_out, OP5);
  and and_4 (MemWrite, OP0, OP1, not_13_out, OP3, not_14_out, OP5);
  and and_5 (and_5_out, not_15_out, not_16_out, not_17_out, not_18_out, OP5);
  and and_6 (and_6_out, not_19_out, OP3, not_20_out, not_21_out);
  and and_7 (and_7_out, not_22_out, OP3, not_23_out, not_24_out);
  and and_8 (and_8_out, not_25_out, OP3, not_26_out, not_27_out);
  and and_9 (and_9_out, OP0, OP1, not_28_out, not_29_out, OP5);
  and and_10 (and_10_out, not_30_out, not_31_out, not_32_out, not_33_out, not_34_out, not_35_out, not_36_out, not_37_out, not_38_out);
  and and_11 (and_11_out, not_39_out, not_40_out, not_41_out, not_42_out, not_43_out, F1, not_44_out, not_45_out, not_46_out);
  and and_12 (and_12_out, not_47_out, not_48_out, not_49_out, not_50_out, not_51_out, F1, not_52_out, not_53_out, F5);
  and and_13 (and_13_out, not_54_out, not_55_out, not_56_out, not_57_out, not_58_out, F0, not_59_out, not_60_out, F5);
  and and_14 (and_14_out, not_61_out, not_62_out, not_63_out, not_64_out, OP5);
  and and_15 (and_15_out, not_65_out, OP3, not_66_out, not_67_out);
  and and_16 (and_16_out, not_68_out, OP3, not_69_out, not_70_out);
  and and_17 (and_17_out, not_71_out, OP3, not_72_out, not_73_out);
  and and_18 (and_18_out, OP0, OP1, not_74_out, not_75_out, not_76_out);
  and and_19 (SysCALL, not_77_out, not_78_out, not_79_out, not_80_out, not_81_out, not_82_out, not_83_out, not_84_out, F2, F3, not_85_out, not_86_out);
  and and_20 (and_20_out, not_87_out, not_88_out, not_89_out, not_90_out, OP5);
  and and_21 (and_21_out, not_91_out, not_92_out, OP3, not_93_out, not_94_out);
  and and_22 (and_22_out, not_95_out, not_96_out, OP3, not_97_out, not_98_out);
  and and_23 (and_23_out, OP0, OP1, not_99_out, not_100_out, OP5);
  and and_24 (and_24_out, not_101_out, not_102_out, not_103_out, not_104_out, not_105_out, not_106_out, not_107_out, not_108_out, not_109_out, not_110_out);
  and and_25 (and_25_out, not_111_out, not_112_out, not_113_out, not_114_out, not_115_out, not_116_out, F1, not_117_out, not_118_out, not_119_out);
  and and_26 (and_26_out, not_120_out, not_121_out, not_122_out, not_123_out, not_124_out, not_125_out, F1, not_126_out, not_127_out, F5);
  and and_27 (and_27_out, not_128_out, not_129_out, not_130_out, not_131_out, not_132_out, not_133_out, F0, not_134_out, not_135_out, F5);
  and and_28 (BEQ, not_136_out, not_137_out, OP2, not_138_out, not_139_out, not_140_out);
  and and_29 (BNE, OP0, not_141_out, OP2, not_142_out, not_143_out, not_144_out);
  and and_30 (JR, not_145_out, not_146_out, not_147_out, not_148_out, not_149_out, not_150_out, not_151_out, not_152_out, not_153_out, F3, not_154_out, not_155_out);
  and and_31 (and_31_out, not_156_out, not_157_out, not_158_out, not_159_out, not_160_out, not_161_out, not_162_out, not_163_out, F3, not_164_out, not_165_out);
  and and_32 (and_32_out, OP1, not_166_out, not_167_out, not_168_out, not_169_out);
  and and_33 (JAL, OP0, OP1, not_170_out, not_171_out, not_172_out, not_173_out);
  or or_1 (MemToReg, and_1_out, and_2_out, and_3_out);
  or or_2 (ALU_SRC, and_5_out, and_6_out, and_7_out, and_8_out, and_9_out);
  or or_3 (RegWrite, and_10_out, and_11_out, and_12_out, and_13_out, and_14_out, and_15_out, and_16_out, and_17_out, and_18_out);
  or or_4 (SignedExt, and_20_out, and_21_out, and_22_out, and_23_out);
  or or_5 (RegDst, and_24_out, and_25_out, and_26_out, and_27_out);
  or or_6 (JMP, and_31_out, and_32_out);
endmodule

// ALU
module MIPS_ALU (
  input  [4:0] shamt,
  input  [31:0] X,
  input  [31:0] Y,
  input  [3:0] AluOP,
  output Equal,
  output [31:0] Result,
  output [31:0] Result_2
);

  wire [0:0] comparator_1_lt, comparator_2_lt;
  wire [31:0] adder_1_out, AND_out, divider_1_out, divider_1_rem, multiplier_1_cout, multiplier_1_out,
       NOR_out, OR_out, shifter_1_out, shifter_2_out, shifter_3_out, subtractor_1_out, XOR_out;

  assign AND_out = X & Y;  // AND_Gate AND, 32 bits wide
  assign OR_out = X | Y;  // OR_Gate OR, 32 bits wide
  Shifter #(.width(32), .shift("ll")) shifter_1 (.in(Y), .\dist (shamt), .out(shifter_1_out));
  Shifter #(.width(32), .shift("ar")) shifter_2 (.in(Y), .\dist (shamt), .out(shifter_2_out));
  Shifter #(.width(32), .shift("lr")) shifter_3 (.in(Y), .\dist (shamt), .out(shifter_3_out));
  Multiplier #(.width(32)) multiplier_1 (.a(X), .b(Y), .out(multiplier_1_out), .cout(multiplier_1_cout));  // open: cin
  Divider #(.width(32)) divider_1 (.a(X), .b(Y), .out(divider_1_out), .rem(divider_1_rem));  // open: upper
  Adder #(.width(32)) adder_1 (.a(X), .b(Y), .out(adder_1_out));  // open: cin, cout
  Subtractor #(.width(32)) subtractor_1 (.a(X), .b(Y), .out(subtractor_1_out));  // open: bin, bout
  assign XOR_out = X ^ Y;  // XOR_Gate XOR, 32 bits wide
  assign NOR_out = ~(X | Y);  // NOR_Gate NOR, 32 bits wide
  Comparator #(.width(32), .mode("twosComplement")) comparator_1 (
    .a(X), .b(Y), .eq(Equal), .lt(comparator_1_lt[0]));  // open: gt
  Comparator #(.width(32), .mode("unsigned")) comparator_2 (.a(X), .b(Y), .lt(comparator_2_lt[0]));  // open: gt, eq
  Multiplexer #(.select(4), .width(32), .disabled("Z"), .enable("false")) multiplexer_1 (
    .in0(shifter_1_out), .in1(shifter_2_out), .in2(shifter_3_out), .in3(multiplier_1_out),
    .in4(divider_1_out), .in5(adder_1_out), .in6(subtractor_1_out), .in7(AND_out), .in8(OR_out),
    .in9(XOR_out), .in10(NOR_out), .in11({{31{1'b0}}, comparator_1_lt[0]}),
    .in12({{31{1'b0}}, comparator_2_lt[0]}), .in13({32{1'b0}}), .in14({32{1'b0}}), .in15({32{1'b0}}),
    .out(Result), .sel(AluOP));
  Multiplexer #(.select(4), .width(32), .disabled("Z"), .enable("false")) multiplexer_2 (
    .in0({32{1'b0}}), .in1({32{1'b0}}), .in2({32{1'b0}}), .in3(multiplier_1_cout), .in4(divider_1_rem),
    .in5({32{1'b0}}), .in6({32{1'b0}}), .in7({32{1'b0}}), .in8({32{1'b0}}), .in9({32{1'b0}}),
    .in10({32{1'b0}}), .in11({32{1'b0}}), .in12({32{1'b0}}), .in13({32{1'b0}}), .in14({32{1'b0}}),
    .in15({32{1'b0}}), .out(Result_2), .sel(AluOP));

  // Other names for the same wires on the sheet: Result2[31:0] = Result_2; S[3:0] = AluOP

  // Notes on the sheet:
  //   不要改变此引脚区域内容，也不要改变ALU封装形式
  //   输入引脚
  //   输出引脚
endmodule

module MIPS_Regifile (
  input  [31:0] Din,
  input  Clk,
  input  WE,
  input  [4:0] R1_num,
  input  [4:0] W_num,
  input  [4:0] R2_num,
  output [31:0] R1,
  output [31:0] R2
);

  // RegisterFile registerfile_1: pin names not known; wires that end beside it: Din, Clk, WE, W_num, R1_num, R2_num, R1, R2
endmodule

module \理想流水线  (
);

  wire CLK, Go, IR1, IR2, IR3, RST, W1, W2, W3;
  wire [11:0] EX_PC, ID_PC, IF_PC, MEM_PC, WB_PC;
  wire [15:0] \LoadUse次数 , \总周期数 , \插入气泡数 , \无条件分支数 , \条件分支成功数 ;
  wire [31:0] LedData;

  Button \u_总复位  (.out(RST));
  Button _1 (.out(IR1));
  Button _2 (.out(IR2));
  Button _3 (.out(IR3));
  Button \u_继续运行  (.out(Go));
  LED #(.active("true")) led_1 (.in(W1));
  LED #(.active("true")) led_2 (.in(W2));
  LED #(.active("true")) led_3 (.in(W3));
  Hex_Digit_Display hex_digit_display_1 (.value(LedData[31:28]));  // open: dp
  Hex_Digit_Display hex_digit_display_2 (.value(LedData[27:24]));  // open: dp
  Hex_Digit_Display hex_digit_display_3 (.value(LedData[23:20]));  // open: dp
  Hex_Digit_Display hex_digit_display_4 (.value(LedData[19:16]));  // open: dp
  Hex_Digit_Display hex_digit_display_5 (.value(LedData[15:12]));  // open: dp
  Hex_Digit_Display hex_digit_display_6 (.value(LedData[7:4]));  // open: dp
  Hex_Digit_Display hex_digit_display_7 (.value(LedData[11:8]));  // open: dp
  Clock #(.highDuration(1), .lowDuration(1)) clock_1 (.out(CLK));
  Hex_Digit_Display hex_digit_display_8 (.value(LedData[3:0]));  // open: dp
  // Probe on \总周期数 
  // Probe on \无条件分支数 
  // Probe on \条件分支成功数 
  // Probe on \插入气泡数 
  // Probe on \LoadUse次数 
  // Probe on IF_PC
  // Probe on EX_PC
  // Probe on ID_PC
  // Probe on MEM_PC
  // Probe on WB_PC

  // Notes on the sheet:
  //   中断源
  //   中断等待指示
  //   数码管输出
  //   流水调试日志用
endmodule

module \气泡流水线  (
  output RegWrite,
  output MemWrite,
  output [31:0] PC,
  output [31:0] IR,
  output [31:0] RDin,
  output [31:0] MDin
);

  wire CLK, Go, IR1, IR2, IR3, W1, W2, W3;
  wire [15:0] \总周期数 ;
  wire [31:0] LedData;

  Clock #(.highDuration(1), .lowDuration(1)) clock_1 (.out(CLK));
  Button _1 (.out(IR1));
  Button _2 (.out(IR2));
  Button _3 (.out(IR3));
  Button \u_继续运行  (.out(Go));
  LED #(.active("true")) led_1 (.in(W1));
  LED #(.active("true")) led_2 (.in(W2));
  LED #(.active("true")) led_3 (.in(W3));
  Hex_Digit_Display hex_digit_display_1 (.value(LedData[31:28]));  // open: dp
  Hex_Digit_Display hex_digit_display_2 (.value(LedData[23:20]));  // open: dp
  Hex_Digit_Display hex_digit_display_3 (.value(LedData[27:24]));  // open: dp
  Hex_Digit_Display hex_digit_display_4 (.value(LedData[15:12]));  // open: dp
  Hex_Digit_Display hex_digit_display_5 (.value(LedData[19:16]));  // open: dp
  Hex_Digit_Display hex_digit_display_6 (.value(LedData[7:4]));  // open: dp
  Hex_Digit_Display hex_digit_display_7 (.value(LedData[11:8]));  // open: dp
  // Probe on \总周期数 
  Hex_Digit_Display hex_digit_display_8 (.value(LedData[3:0]));  // open: dp

  // Notes on the sheet:
  //   中断源
  //   中断等待指示
  //   总复位信号应将除ROM以外所有存储组件全部清零
  //   数码管输出
  //   数码管输出应该用寄存器锁存，否则显示数据只能一闪而过
  //   为方便自动评测，需要输出PC，IR，寄存器文件写入端口RDin，内存写入端口MDin等信号
endmodule

module \重定向流水线  (
  output RegWrite,
  output MemWrite,
  output [31:0] PC,
  output [31:0] IR,
  output [31:0] RDin,
  output [31:0] MDin
);

  wire CLK, Go, IR1, IR2, IR3, W1, W2, W3;
  wire [15:0] \总周期数 ;
  wire [31:0] LedData;

  Clock #(.highDuration(1), .lowDuration(1)) clock_1 (.out(CLK));
  Button _1 (.out(IR1));
  Button _2 (.out(IR2));
  Button _3 (.out(IR3));
  Button \u_继续运行  (.out(Go));
  LED #(.active("true")) led_1 (.in(W1));
  LED #(.active("true")) led_2 (.in(W2));
  LED #(.active("true")) led_3 (.in(W3));
  Hex_Digit_Display hex_digit_display_1 (.value(LedData[31:28]));  // open: dp
  Hex_Digit_Display hex_digit_display_2 (.value(LedData[27:24]));  // open: dp
  Hex_Digit_Display hex_digit_display_3 (.value(LedData[23:20]));  // open: dp
  Hex_Digit_Display hex_digit_display_4 (.value(LedData[15:12]));  // open: dp
  Hex_Digit_Display hex_digit_display_5 (.value(LedData[19:16]));  // open: dp
  Hex_Digit_Display hex_digit_display_6 (.value(LedData[11:8]));  // open: dp
  Hex_Digit_Display hex_digit_display_7 (.value(LedData[7:4]));  // open: dp
  // Probe on \总周期数 
  Hex_Digit_Display hex_digit_display_8 (.value(LedData[3:0]));  // open: dp

  // Notes on the sheet:
  //   中断源
  //   中断等待指示
  //   总复位信号应将除ROM以外所有存储组件全部清零
  //   数码管输出
  //   数码管输出应该用寄存器锁存，否则显示数据只能一闪而过
  //   为方便自动评测，需要输出PC，IR，寄存器文件写入端口RDin，内存写入端口MDin等信号
endmodule

module \中断按键参考电路  (
  input  \同步清零信号 ,
  output \与中断屏蔽位与 
);

  wire \_1号中断_out , and_1_out, clock_1_out, d_ff_1_q, or_1_out, or_2_out;

  Clock #(.highDuration(1), .lowDuration(1)) clock_1 (.out(clock_1_out));
  Button \_1号中断  (.out(\_1号中断_out ));
  LED #(.active("true")) \_1号中断等待指示灯  (.in(or_1_out));
  or or_1 (or_1_out, \与中断屏蔽位与 , d_ff_1_q);
  D_Flip_Flop #(.trigger("rising"), .Pre_Clr_Positions("LEGACY"), .NegatePresetClear("false"), .enable("true"), .NewFFLayout("false")) d_ff_1 (
    .clk(\_1号中断_out ), .D(1'b1), .Q(d_ff_1_q), .reset(\与中断屏蔽位与 ));  // open: Qn, preset, en
  or or_2 (or_2_out, d_ff_1_q, \与中断屏蔽位与 );
  and and_1 (and_1_out, or_2_out, ~\同步清零信号 );  // AND_Gate
  D_Flip_Flop #(.trigger("rising"), .Pre_Clr_Positions("LEGACY"), .NegatePresetClear("false"), .enable("true"), .NewFFLayout("false")) IR1 (
    .clk(clock_1_out), .D(and_1_out), .Q(\与中断屏蔽位与 ));  // open: Qn, preset, en, reset
  \单周期硬布线控制器  \u_单周期硬布线控制器_1  ();  // open: Func, OP, ALU_OP, MemToReg, MemWrite, ALU_SRC, RegWrite, SysCALL, SignedExt, RegDst, JR, JMP, Beq, JAL, Bne

  // Notes on the sheet:
  //   中断信号采样参考电路
  //   Reset 
endmodule

module NEW_CONTRLLER (
  input  OP0,
  input  OP1,
  input  OP2,
  input  OP3,
  input  OP4,
  input  OP5,
  input  F0,
  input  F1,
  input  F2,
  input  F3,
  input  F4,
  input  F5,
  output byteorword,
  output bltz,
  output ALutoREg
);

  wire not_1_out, not_2_out, not_3_out, not_4_out, not_5_out, not_6_out, not_7_out, not_8_out, not_9_out,
       not_10_out, not_11_out, not_12_out, not_13_out;

  not not_1 (not_1_out, OP0);
  not not_2 (not_2_out, OP1);
  not not_3 (not_3_out, OP2);
  not not_4 (not_4_out, OP3);
  not not_5 (not_5_out, OP4);
  not not_6 (not_6_out, OP1);
  not not_7 (not_7_out, OP2);
  not not_8 (not_8_out, OP3);
  not not_9 (not_9_out, OP4);
  not not_10 (not_10_out, OP5);
  not not_11 (not_11_out, OP2);
  not not_12 (not_12_out, OP4);
  not not_13 (not_13_out, OP5);
  and and_1 (byteorword, not_1_out, not_2_out, not_3_out, not_4_out, not_5_out, OP5);
  and and_2 (bltz, OP0, not_6_out, not_7_out, not_8_out, not_9_out, not_10_out);
  and and_3 (ALutoREg, OP0, OP1, not_11_out, OP3, not_12_out, not_13_out);
endmodule
